# Fritzing sketch mina fritzing onebutton (saved by Fritzing 0.9.4)
breadboards: 1

parts:
  LED1 = smd LED [color="Red (633nm)" package="0805 [SMD]"]
  S1 = Pushbutton [package="[THT]"]
  R1 = Resistor [tolerance=±5% resistance=220 package="2010 [SMD]"]
  R2 = Resistor [tolerance=±5% resistance=220 package="2010 [SMD]"]
  Teensy_3_1 = Teensy 3.1  # not connected

nets:
  N1: LED1.cathode, R1.Pin_0
  N2: S1.Pin_1, S1.Pin_2
  N3: S1.Pin_3, S1.Pin_4, R2.Pin_0
  N4: R1.Pin_1, R2.Pin_1
